# Fritzing sketch Final project Fritzing (saved by Fritzing 0.7.12b)
breadboards: 1

parts:
  Arduino1 = Arduino
  VCC1 = Battery
  J1 = Basic Servo
  J2 = Basic Servo
  J3 = Piezo Speaker
  LED1 = LED - 5mm [color="Red (633nm)" package="5 mm [THT]"]
  LED2 = LED - 5mm [color="Red (633nm)" package="5 mm [THT]"]
  R1 = Resistor [tolerance=±5% resistance=220 package=THT]
  R2 = Resistor [tolerance=±5% resistance=220 package=THT]
  R3 = Resistor [tolerance=±5% resistance=220 package=THT]
  R4 = Photocell (LDR) [package=THT]  # not connected
  R5 = Resistor [tolerance=±5% resistance=220 package=THT]
  R6 = Resistor [tolerance=±5% resistance=220 package=THT]
  R7 = Photocell (LDR) [package=THT]

nets:
  N1: Arduino1.D10, J1.pulse
  N2: Arduino1.D9, J2.pulse
  N3: Arduino1.+5V, J3.pin1, J3.pin2, LED1.anode, LED2.anode, R1.Pin_1
  GND: Arduino1.GND, VCC1.-, J1.gnd, J2.gnd, R1.Pin_0, R2.Pin_0, R3.Pin_0, R5.Pin_0, R6.Pin_0
  VCC: VCC1.+, J1.vcc, J2.vcc
  N4: LED1.cathode, R2.Pin_1
  N5: LED2.cathode, R3.Pin_1
  N6: R6.Pin_1, R7.pin_0
